// Digital circuit ALU.dig as structural Verilog
module ALU (
  input  [7:0] AC,
  input  [7:0] N,
  input  [2:0] Opcode,
  input  [2:0] Alt,
  output [7:0] MQ,
  output [7:0] AC_out
);

  wire [7:0] _000, _001, _010, _011, _100, _101, _110, _111, MQ0, MQ1;

  somador8bits somador8bits_1 (.A(AC), .B(N), .S(_000));
  subtrator8bits subtrator8bits_1 (.B(N), .A(AC), .S(_001));
  // multiplicador multiplicador_1: pin names not known; wires that end beside it: AC, N, _010, MQ0
  divisor8bits divisor8bits_1 (.A(AC), .B(N), .R(_011), .Q(MQ1));
  shiftleft shiftleft_1 (.Entrada(AC), .S(_100));
  shiftright shiftright_1 (.Entrada(AC), .\Saída (_101));
  NAND nand_1 (.A(AC), .B(N), .S(_110));
  XOR xor_1 (.A(AC), .B(N), .S(_111));
  Multiplexer #(.Selector_Bits(3), .Bits(8)) multiplexer_1 (
    .sel(Opcode), .in_0(_000), .in_1(_001), .in_2(_010), .in_3(_011), .in_4(_100), .in_5(_101), .in_6(_110),
    .in_7(_111), .out(AC_out));
  Multiplexer #(.Selector_Bits(3), .Bits(8)) multiplexer_2 (
    .sel(Alt), .in_0({8{1'b0}}), .in_1({8{1'b0}}), .in_2(MQ0), .in_3(MQ1), .in_4({8{1'b0}}),
    .in_5({8{1'b0}}), .in_6({8{1'b0}}), .in_7({8{1'b0}}), .out(MQ));
endmodule
