// Digital circuit CPU.dig as structural Verilog
module CPU (
  input  ENABLE,
  input  clk,
  input  [7:0] N,
  input  [2:0] Opcode,
  output [7:0] out_5,
  output [7:0] out_6
);

  wire [7:0] alu_1_ac_out, alu_1_mq;

  ALU alu_1 (.AC(out_5), .N(N), .Opcode(Opcode), .Alt(3'b000), .MQ(alu_1_mq), .AC_out(alu_1_ac_out));
  Register #(.Bits(8)) register_1 (.D(alu_1_mq), .C(clk), .en(ENABLE), .Q(out_6));
  Register #(.Bits(8)) register_2 (.D(alu_1_ac_out), .C(clk), .en(ENABLE), .Q(out_5));

  // Other names for the same wires on the sheet: AC[7:0] = out_5; EN = ENABLE; MQ[7:0] = out_6
endmodule
