// Digital circuit SOMA1BIT.dig as structural Verilog
module SOMA1BIT (
  input  a,
  input  b,
  input  Cin,
  output Cout,
  output S
);

  wire and_1_out, and_2_out, and_3_out, and_4_out, and_5_out, and_6_out, and_7_out, not_1_out, not_2_out,
       not_3_out;

  not not_1 (not_1_out, a);
  not not_2 (not_2_out, b);
  not not_3 (not_3_out, Cin);
  and and_1 (and_1_out, not_1_out, Cin, not_2_out);
  and and_2 (and_2_out, not_1_out, b, not_3_out);
  and and_3 (and_3_out, a, b, Cin);
  and and_4 (and_4_out, not_3_out, not_2_out, a);
  and and_5 (and_5_out, a, b);
  and and_6 (and_6_out, a, Cin);
  and and_7 (and_7_out, b, Cin);
  or or_1 (S, and_1_out, and_2_out, and_3_out, and_4_out);
  or or_2 (Cout, and_5_out, and_6_out, and_7_out);
endmodule
