// Digital circuit divisor8bits.dig as structural Verilog
module divisor8bits (
  input  [7:0] A,
  input  [7:0] B,
  output [7:0] R,
  output [7:0] Q
);

  wire r0_t, r1_t, r2_t, r3_t, r4_t, r5_t, r6_t, r7_t, r8, r9, r10, r11, r12, r13, r14, r15, r16, r17, r18,
       r19, r20, r21, r22, r23, r24, r25, r26, r27, r28, r29, r30, r31, r32, r33, r34, r35, r36, r37, r38,
       r39, r40, r41, r42, r43, r44, r45, r46, r47, r48, subrestore_1_r, subrestore_2_cout, subrestore_3_r,
       subrestore_4_r, subrestore_5_cout, subrestore_6_cout, subrestore_7_cout, subrestore_8_r,
       subrestore_9_cout, subrestore_10_cout, subrestore_11_cout, subrestore_12_cout, subrestore_13_r,
       subrestore_14_cout, subrestore_15_cout, subrestore_16_cout, subrestore_17_cout, subrestore_18_cout,
       subrestore_19_r, subrestore_20_cout, subrestore_21_cout, subrestore_22_cout, subrestore_23_cout,
       subrestore_24_cout, subrestore_25_cout, subrestore_26_r, subrestore_27_cout, subrestore_28_cout,
       subrestore_29_cout, subrestore_30_cout, subrestore_31_cout, subrestore_32_cout, subrestore_33_cout,
       subrestore_35_cout, subrestore_36_cout, subrestore_37_cout, subrestore_38_cout, subrestore_39_cout,
       subrestore_40_cout, subrestore_41_cout, subrestore_42_cout, subrestore_43_cout, subrestore_44_cout,
       subrestore_45_cout, subrestore_46_cout, subrestore_47_cout, subrestore_48_cout, subrestore_49_cout,
       subrestore_50_cout, subrestore_51_cout, subrestore_52_cout, subrestore_53_cout, subrestore_54_cout,
       subrestore_55_cout, subrestore_56_cout, subrestore_57_cout, subrestore_58_cout, subrestore_59_cout,
       subrestore_60_cout, subrestore_61_cout, subrestore_62_cout, subrestore_63_cout, subrestore_64_cout;

  subrestore subrestore_1 (.A(1'b0), .B(B[7]), .Cin(subrestore_2_cout), .S(Q[7]), .R(subrestore_1_r), .Cout(Q[7]));
  subrestore subrestore_2 (.A(1'b0), .B(B[6]), .Cin(subrestore_5_cout), .S(Q[7]), .R(r6_t), .Cout(subrestore_2_cout));
  subrestore subrestore_3 (.A(r6_t), .B(B[7]), .Cin(subrestore_6_cout), .S(Q[6]), .R(subrestore_3_r), .Cout(Q[6]));
  subrestore subrestore_4 (.A(r13), .B(B[7]), .Cin(subrestore_7_cout), .S(Q[5]), .R(subrestore_4_r), .Cout(Q[5]));
  subrestore subrestore_5 (.A(1'b0), .B(B[5]), .Cin(subrestore_9_cout), .S(Q[7]), .R(r5_t), .Cout(subrestore_5_cout));
  subrestore subrestore_6 (.A(r5_t), .B(B[6]), .Cin(subrestore_10_cout), .S(Q[6]), .R(r13), .Cout(subrestore_6_cout));
  subrestore subrestore_7 (.A(r12), .B(B[6]), .Cin(subrestore_11_cout), .S(Q[5]), .R(r20), .Cout(subrestore_7_cout));
  subrestore subrestore_8 (.A(r20), .B(B[7]), .Cin(subrestore_12_cout), .S(Q[4]), .R(subrestore_8_r), .Cout(Q[4]));
  subrestore subrestore_9 (.A(1'b0), .B(B[4]), .Cin(subrestore_14_cout), .S(Q[7]), .R(r4_t), .Cout(subrestore_9_cout));
  subrestore subrestore_10 (.A(r4_t), .B(B[5]), .Cin(subrestore_15_cout), .S(Q[6]), .R(r12), .Cout(subrestore_10_cout));
  subrestore subrestore_11 (.A(r11), .B(B[5]), .Cin(subrestore_16_cout), .S(Q[5]), .R(r19), .Cout(subrestore_11_cout));
  subrestore subrestore_12 (.A(r19), .B(B[6]), .Cin(subrestore_17_cout), .S(Q[4]), .R(r27), .Cout(subrestore_12_cout));
  subrestore subrestore_13 (.A(r27), .B(B[7]), .Cin(subrestore_18_cout), .S(Q[3]), .R(subrestore_13_r), .Cout(Q[3]));
  subrestore subrestore_14 (
    .A(1'b0), .B(B[3]), .Cin(subrestore_20_cout), .S(Q[7]), .R(r3_t), .Cout(subrestore_14_cout));
  subrestore subrestore_15 (.A(r3_t), .B(B[4]), .Cin(subrestore_21_cout), .S(Q[6]), .R(r11), .Cout(subrestore_15_cout));
  subrestore subrestore_16 (.A(r10), .B(B[4]), .Cin(subrestore_22_cout), .S(Q[5]), .R(r18), .Cout(subrestore_16_cout));
  subrestore subrestore_17 (.A(r18), .B(B[5]), .Cin(subrestore_23_cout), .S(Q[4]), .R(r26), .Cout(subrestore_17_cout));
  subrestore subrestore_18 (.A(r26), .B(B[6]), .Cin(subrestore_24_cout), .S(Q[3]), .R(r34), .Cout(subrestore_18_cout));
  subrestore subrestore_19 (.A(r34), .B(B[7]), .Cin(subrestore_25_cout), .S(Q[2]), .R(subrestore_19_r), .Cout(Q[2]));
  subrestore subrestore_20 (
    .A(1'b0), .B(B[2]), .Cin(subrestore_27_cout), .S(Q[7]), .R(r2_t), .Cout(subrestore_20_cout));
  subrestore subrestore_21 (.A(r2_t), .B(B[3]), .Cin(subrestore_28_cout), .S(Q[6]), .R(r10), .Cout(subrestore_21_cout));
  subrestore subrestore_22 (.A(r9), .B(B[3]), .Cin(subrestore_29_cout), .S(Q[5]), .R(r17), .Cout(subrestore_22_cout));
  subrestore subrestore_23 (.A(r17), .B(B[4]), .Cin(subrestore_30_cout), .S(Q[4]), .R(r25), .Cout(subrestore_23_cout));
  subrestore subrestore_24 (.A(r25), .B(B[5]), .Cin(subrestore_31_cout), .S(Q[3]), .R(r33), .Cout(subrestore_24_cout));
  subrestore subrestore_25 (.A(r33), .B(B[6]), .Cin(subrestore_32_cout), .S(Q[2]), .R(r41), .Cout(subrestore_25_cout));
  subrestore subrestore_26 (.A(r41), .B(B[7]), .Cin(subrestore_33_cout), .S(Q[1]), .R(subrestore_26_r), .Cout(Q[1]));
  subrestore subrestore_27 (
    .A(1'b0), .B(B[1]), .Cin(subrestore_35_cout), .S(Q[7]), .R(r1_t), .Cout(subrestore_27_cout));
  subrestore subrestore_28 (.A(r1_t), .B(B[2]), .Cin(subrestore_36_cout), .S(Q[6]), .R(r9), .Cout(subrestore_28_cout));
  subrestore subrestore_29 (.A(r8), .B(B[2]), .Cin(subrestore_37_cout), .S(Q[5]), .R(r16), .Cout(subrestore_29_cout));
  subrestore subrestore_30 (.A(r16), .B(B[3]), .Cin(subrestore_38_cout), .S(Q[4]), .R(r24), .Cout(subrestore_30_cout));
  subrestore subrestore_31 (.A(r24), .B(B[4]), .Cin(subrestore_39_cout), .S(Q[3]), .R(r32), .Cout(subrestore_31_cout));
  subrestore subrestore_32 (.A(r32), .B(B[5]), .Cin(subrestore_40_cout), .S(Q[2]), .R(r40), .Cout(subrestore_32_cout));
  subrestore subrestore_33 (.A(r40), .B(B[6]), .Cin(subrestore_41_cout), .S(Q[1]), .R(r48), .Cout(subrestore_33_cout));
  subrestore subrestore_34 (.A(r48), .B(B[7]), .Cin(subrestore_42_cout), .S(Q[0]), .R(R[7]), .Cout(Q[0]));
  subrestore subrestore_35 (.A(A[7]), .B(B[0]), .Cin(1'b1), .S(Q[7]), .R(r0_t), .Cout(subrestore_35_cout));
  subrestore subrestore_36 (.A(r0_t), .B(B[1]), .Cin(subrestore_43_cout), .S(Q[6]), .R(r8), .Cout(subrestore_36_cout));
  subrestore subrestore_37 (.A(r7_t), .B(B[1]), .Cin(subrestore_44_cout), .S(Q[5]), .R(r15), .Cout(subrestore_37_cout));
  subrestore subrestore_38 (.A(r15), .B(B[2]), .Cin(subrestore_45_cout), .S(Q[4]), .R(r23), .Cout(subrestore_38_cout));
  subrestore subrestore_39 (.A(r23), .B(B[3]), .Cin(subrestore_46_cout), .S(Q[3]), .R(r31), .Cout(subrestore_39_cout));
  subrestore subrestore_40 (.A(r31), .B(B[4]), .Cin(subrestore_47_cout), .S(Q[2]), .R(r39), .Cout(subrestore_40_cout));
  subrestore subrestore_41 (.A(r39), .B(B[5]), .Cin(subrestore_48_cout), .S(Q[1]), .R(r47), .Cout(subrestore_41_cout));
  subrestore subrestore_42 (.A(r47), .B(B[6]), .Cin(subrestore_49_cout), .S(Q[0]), .R(R[6]), .Cout(subrestore_42_cout));
  subrestore subrestore_43 (.A(A[6]), .B(B[0]), .Cin(1'b1), .S(Q[6]), .R(r7_t), .Cout(subrestore_43_cout));
  subrestore subrestore_44 (.A(A[5]), .B(B[0]), .Cin(1'b1), .S(Q[5]), .R(r14), .Cout(subrestore_44_cout));
  subrestore subrestore_45 (.A(r14), .B(B[1]), .Cin(subrestore_50_cout), .S(Q[4]), .R(r22), .Cout(subrestore_45_cout));
  subrestore subrestore_46 (.A(r22), .B(B[2]), .Cin(subrestore_51_cout), .S(Q[3]), .R(r30), .Cout(subrestore_46_cout));
  subrestore subrestore_47 (.A(r30), .B(B[3]), .Cin(subrestore_52_cout), .S(Q[2]), .R(r38), .Cout(subrestore_47_cout));
  subrestore subrestore_48 (.A(r38), .B(B[4]), .Cin(subrestore_53_cout), .S(Q[1]), .R(r46), .Cout(subrestore_48_cout));
  subrestore subrestore_49 (.A(r46), .B(B[5]), .Cin(subrestore_54_cout), .S(Q[0]), .R(R[5]), .Cout(subrestore_49_cout));
  subrestore subrestore_50 (.A(A[4]), .B(B[0]), .Cin(1'b1), .S(Q[4]), .R(r21), .Cout(subrestore_50_cout));
  subrestore subrestore_51 (.A(r21), .B(B[1]), .Cin(subrestore_55_cout), .S(Q[3]), .R(r29), .Cout(subrestore_51_cout));
  subrestore subrestore_52 (.A(r29), .B(B[2]), .Cin(subrestore_56_cout), .S(Q[2]), .R(r37), .Cout(subrestore_52_cout));
  subrestore subrestore_53 (.A(r37), .B(B[3]), .Cin(subrestore_57_cout), .S(Q[1]), .R(r45), .Cout(subrestore_53_cout));
  subrestore subrestore_54 (.A(r45), .B(B[4]), .Cin(subrestore_58_cout), .S(Q[0]), .R(R[4]), .Cout(subrestore_54_cout));
  subrestore subrestore_55 (.A(A[3]), .B(B[0]), .Cin(1'b1), .S(Q[3]), .R(r28), .Cout(subrestore_55_cout));
  subrestore subrestore_56 (.A(r28), .B(B[1]), .Cin(subrestore_59_cout), .S(Q[2]), .R(r36), .Cout(subrestore_56_cout));
  subrestore subrestore_57 (.A(r36), .B(B[2]), .Cin(subrestore_60_cout), .S(Q[1]), .R(r44), .Cout(subrestore_57_cout));
  subrestore subrestore_58 (.A(r44), .B(B[3]), .Cin(subrestore_61_cout), .S(Q[0]), .R(R[3]), .Cout(subrestore_58_cout));
  subrestore subrestore_59 (.A(A[2]), .B(B[0]), .Cin(1'b1), .S(Q[2]), .R(r35), .Cout(subrestore_59_cout));
  subrestore subrestore_60 (.A(r35), .B(B[1]), .Cin(subrestore_62_cout), .S(Q[1]), .R(r43), .Cout(subrestore_60_cout));
  subrestore subrestore_61 (.A(r43), .B(B[2]), .Cin(subrestore_63_cout), .S(Q[0]), .R(R[2]), .Cout(subrestore_61_cout));
  subrestore subrestore_62 (.A(A[1]), .B(B[0]), .Cin(1'b1), .S(Q[1]), .R(r42), .Cout(subrestore_62_cout));
  subrestore subrestore_63 (.A(r42), .B(B[1]), .Cin(subrestore_64_cout), .S(Q[0]), .R(R[1]), .Cout(subrestore_63_cout));
  subrestore subrestore_64 (.A(A[0]), .B(B[0]), .Cin(1'b1), .S(Q[0]), .R(R[0]), .Cout(subrestore_64_cout));
  // also tied to GND on the sheet: {subrestore_13_r, subrestore_19_r, subrestore_26_r, subrestore_8_r, subrestore_4_r, subrestore_3_r, subrestore_1_r}

  // Other names for the same wires on the sheet: D0 = A[0]; D1 = A[1]; D2 = A[2]; D3 = A[3]; D4 = A[4]; D5 = A[5];
  //   D6 = A[6]; D7 = A[7]; d0_t = B[0]; d1_t = B[1]; d2_t = B[2]; d3_t = B[3]; d4_t = B[4]; d5_t = B[5]; d6_t = B[6];
  //   d7_t = B[7]; Cout7 = Q[0]; Cout6 = Q[1]; Cout5 = Q[2]; Cout4 = Q[3]; Cout3 = Q[4]; Cout2 = Q[5]; Cout1 = Q[6];
  //   Cout0 = Q[7]
endmodule
