// Digital circuit multiplicador.dig as structural Verilog
module multiplicador (
  input  [7:0] A,
  input  [7:0] B,
  output [15:0] P
);

  wire and_1_out, and_2_out, and_3_out, and_4_out, and_5_out, and_6_out, and_7_out, and_9_out, and_10_out,
       and_11_out, and_12_out, and_13_out, and_14_out, and_15_out, and_16_out, and_17_out, and_18_out,
       and_19_out, and_20_out, and_21_out, and_22_out, and_23_out, and_24_out, and_25_out, and_26_out,
       and_27_out, and_28_out, and_31_out, and_32_out, and_33_out, and_34_out, and_35_out, and_36_out,
       and_38_out, and_39_out, and_40_out, and_41_out, and_42_out, and_43_out, and_44_out, and_45_out,
       and_46_out, and_47_out, and_48_out, and_49_out, and_50_out, and_51_out, and_52_out, and_53_out,
       and_54_out, and_55_out, and_58_out, and_59_out, and_60_out, and_61_out, and_62_out, and_63_out,
       fa_1_p1, fa_1_p4, fa_2_p2, fa_2_p4, fa_2_p5, fa_3_p1, fa_4_p3, fa_4_p4, fa_4_p5, fa_5_p1, fa_5_p3,
       fa_6_p1, fa_6_p2, fa_6_p3, fa_6_p4, fa_7_p1, fa_8_p1, fa_8_p4, fa_9_p1, fa_9_p3, fa_10_p2, fa_10_p4,
       fa_10_p5, fa_11_p1, fa_11_p3, fa_12_p1, fa_12_p3, fa_13_p1, fa_14_p3, fa_14_p4, fa_14_p5, fa_15_p1,
       fa_15_p3, fa_16_p1, fa_17_p1, fa_17_p3, fa_18_p1, fa_18_p3, fa_19_p1, fa_19_p3, fa_20_p1, fa_20_p3,
       fa_21_p1, fa_21_p3, fa_22_p1, fa_22_p3, fa_23_p1, fa_24_p1, fa_24_p3, fa_24_p4, fa_24_p5, fa_25_p1,
       fa_25_p3, fa_25_p4, fa_26_p1, fa_26_p3, fa_27_p1, fa_27_p3, fa_28_p1, fa_28_p3, fa_29_p1, fa_29_p3,
       fa_30_p1, fa_30_p2, fa_30_p3, fa_30_p4, fa_31_p1, fa_32_p1, fa_32_p3, fa_33_p1, fa_33_p3, fa_34_p1,
       fa_35_p1, fa_35_p3, fa_36_p1, fa_36_p3, fa_37_p1, fa_37_p3, fa_38_p1, fa_38_p3, fa_39_p1, fa_39_p3,
       fa_40_p1, fa_40_p3, fa_41_p1, fa_41_p3, fa_42_p1, fa_42_p3, fa_43_p1, fa_43_p3, fa_44_p1, fa_44_p3,
       fa_45_p1, fa_45_p3, fa_46_p1, fa_46_p3, fa_46_p4, fa_47_p1, fa_47_p3, fa_47_p4, fa_48_p1, fa_48_p3,
       ha_1_s;

  and and_1 (and_1_out, B[7], A[7]);
  // FA fa_1: pin names not known; wires that end beside it: fa_1_p1, and_1_out, P[15], fa_1_p4, P[14]
  and and_2 (and_2_out, B[6], A[7]);
  // FA fa_2: pin names not known; wires that end beside it: B[7], fa_2_p2, and_2_out, fa_2_p4, fa_2_p5, fa_1_p4
  and and_3 (and_3_out, B[7], A[6]);
  // FA fa_3: pin names not known; wires that end beside it: fa_3_p1, fa_2_p4, P[13], and_3_out, fa_1_p1
  and and_4 (and_4_out, B[5], A[7]);
  // FA fa_4: pin names not known; wires that end beside it: B[6], B[5], fa_4_p3, fa_4_p4, fa_4_p5, and_4_out, fa_2_p5
  and and_5 (and_5_out, B[6], A[6]);
  // FA fa_5: pin names not known; wires that end beside it: fa_5_p1, and_5_out, fa_5_p3, fa_4_p5, fa_2_p2
  and and_6 (and_6_out, B[4], A[7]);
  // FA fa_6: pin names not known; wires that end beside it: fa_6_p1, fa_6_p2, fa_6_p3, fa_6_p4, fa_4_p3
  and and_7 (and_7_out, B[7], A[5]);
  // FA fa_7: pin names not known; wires that end beside it: fa_7_p1, fa_5_p3, P[12], and_7_out, fa_3_p1
  // FA fa_8: pin names not known; wires that end beside it: fa_8_p1, and_6_out, fa_6_p2, fa_8_p4, fa_4_p4
  and and_8 (fa_6_p4, B[5], A[6]);
  and and_9 (and_9_out, B[6], A[5]);
  // FA fa_9: pin names not known; wires that end beside it: fa_9_p1, and_9_out, fa_9_p3, fa_6_p3, fa_5_p1
  and and_10 (and_10_out, B[7], A[4]);
  and and_11 (and_11_out, B[3], A[7]);
  // FA fa_10: pin names not known; wires that end beside it: B[4], fa_10_p2, and_11_out, fa_10_p4, fa_10_p5, fa_8_p4
  and and_12 (and_12_out, B[4], A[6]);
  // FA fa_11: pin names not known; wires that end beside it: fa_11_p1, fa_10_p4, fa_11_p3, and_12_out, fa_8_p1
  and and_13 (and_13_out, B[5], A[5]);
  // FA fa_12: pin names not known; wires that end beside it: fa_12_p1, fa_11_p3, fa_12_p3, and_13_out, fa_6_p1
  // FA fa_13: pin names not known; wires that end beside it: fa_13_p1, fa_9_p3, P[11], and_10_out, fa_7_p1
  and and_14 (and_14_out, B[2], A[7]);
  // FA fa_14: pin names not known; wires that end beside it: B[3], B[2], fa_14_p3, fa_14_p4, fa_14_p5, and_14_out, fa_10_p5
  and and_15 (and_15_out, B[3], A[6]);
  and and_16 (and_16_out, B[6], A[4]);
  // FA fa_15: pin names not known; wires that end beside it: fa_15_p1, and_16_out, fa_15_p3, fa_12_p3, fa_9_p1
  and and_17 (and_17_out, B[7], A[3]);
  // FA fa_16: pin names not known; wires that end beside it: fa_16_p1, fa_15_p3, P[10], and_17_out, fa_13_p1
  and and_18 (and_18_out, A[7], B[1]);
  // FA fa_17: pin names not known; wires that end beside it: fa_17_p1, and_15_out, fa_17_p3, fa_14_p5, fa_10_p2
  and and_19 (and_19_out, B[4], A[5]);
  // FA fa_18: pin names not known; wires that end beside it: fa_18_p1, fa_17_p3, fa_18_p3, and_19_out, fa_11_p1
  and and_20 (and_20_out, B[5], A[4]);
  // FA fa_19: pin names not known; wires that end beside it: fa_19_p1, fa_18_p3, fa_19_p3, and_20_out, fa_12_p1
  and and_21 (and_21_out, B[6], A[3]);
  HA ha_1 (.A(fa_24_p5), .B(and_18_out), .S(ha_1_s), .Cout(fa_14_p4));
  and and_22 (and_22_out, B[2], A[6]);
  // FA fa_20: pin names not known; wires that end beside it: fa_20_p1, ha_1_s, fa_20_p3, and_22_out, fa_14_p3
  and and_23 (and_23_out, B[3], A[5]);
  // FA fa_21: pin names not known; wires that end beside it: fa_21_p1, and_23_out, fa_21_p3, fa_20_p3, fa_17_p1
  // FA fa_22: pin names not known; wires that end beside it: fa_22_p1, and_21_out, fa_22_p3, fa_19_p3, fa_15_p1
  and and_24 (and_24_out, B[7], A[2]);
  // FA fa_23: pin names not known; wires that end beside it: fa_23_p1, fa_22_p3, P[9], and_24_out, fa_16_p1
  and and_25 (and_25_out, B[1], A[6]);
  // FA fa_24: pin names not known; wires that end beside it: fa_24_p1, and_25_out, fa_24_p3, fa_24_p4, fa_24_p5
  // FA fa_25: pin names not known; wires that end beside it: fa_25_p1, fa_24_p3, fa_25_p3, fa_25_p4, fa_20_p1
  and and_26 (and_26_out, B[4], A[4]);
  // FA fa_26: pin names not known; wires that end beside it: fa_26_p1, fa_21_p3, fa_26_p3, and_26_out, fa_18_p1
  and and_27 (and_27_out, B[5], A[3]);
  // FA fa_27: pin names not known; wires that end beside it: fa_27_p1, fa_26_p3, fa_27_p3, and_27_out, fa_19_p1
  and and_28 (and_28_out, B[6], A[2]);
  // FA fa_28: pin names not known; wires that end beside it: fa_28_p1, and_28_out, fa_28_p3, fa_27_p3, fa_22_p1
  and and_29 (fa_24_p4, B[0], A[7]);
  and and_30 (fa_25_p4, B[2], A[5]);
  and and_31 (and_31_out, B[3], A[4]);
  // FA fa_29: pin names not known; wires that end beside it: fa_29_p1, and_31_out, fa_29_p3, fa_25_p3, fa_21_p1
  and and_32 (and_32_out, B[4], A[3]);
  // FA fa_30: pin names not known; wires that end beside it: fa_30_p1, fa_30_p2, fa_30_p3, fa_30_p4, fa_27_p1
  and and_33 (and_33_out, B[7], A[1]);
  // FA fa_31: pin names not known; wires that end beside it: fa_31_p1, fa_28_p3, P[8], and_33_out, fa_23_p1
  and and_34 (and_34_out, B[0], A[6]);
  and and_35 (and_35_out, B[1], A[5]);
  // FA fa_32: pin names not known; wires that end beside it: fa_32_p1, and_35_out, fa_32_p3, and_34_out, fa_24_p1
  and and_36 (and_36_out, B[2], A[4]);
  // FA fa_33: pin names not known; wires that end beside it: fa_33_p1, fa_32_p3, fa_33_p3, and_36_out, fa_25_p1
  // FA fa_34: pin names not known; wires that end beside it: fa_34_p1, fa_29_p3, fa_30_p2, and_32_out, fa_26_p1
  and and_37 (fa_30_p4, B[5], A[2]);
  and and_38 (and_38_out, B[6], A[1]);
  // FA fa_35: pin names not known; wires that end beside it: fa_35_p1, and_38_out, fa_35_p3, fa_30_p3, fa_28_p1
  and and_39 (and_39_out, B[7], A[0]);
  and and_40 (and_40_out, B[3], A[3]);
  // FA fa_36: pin names not known; wires that end beside it: fa_36_p1, and_40_out, fa_36_p3, fa_33_p3, fa_29_p1
  and and_41 (and_41_out, B[4], A[2]);
  // FA fa_37: pin names not known; wires that end beside it: fa_37_p1, fa_36_p3, fa_37_p3, and_41_out, fa_34_p1
  and and_42 (and_42_out, B[5], A[1]);
  // FA fa_38: pin names not known; wires that end beside it: fa_38_p1, fa_37_p3, fa_38_p3, and_42_out, fa_30_p1
  HA ha_2 (.A(and_39_out), .B(fa_35_p3), .S(P[7]), .Cout(fa_31_p1));
  and and_43 (and_43_out, B[0], A[5]);
  and and_44 (and_44_out, B[1], A[4]);
  // FA fa_39: pin names not known; wires that end beside it: fa_39_p1, and_44_out, fa_39_p3, and_43_out, fa_32_p1
  and and_45 (and_45_out, B[2], A[3]);
  // FA fa_40: pin names not known; wires that end beside it: fa_40_p1, fa_39_p3, fa_40_p3, and_45_out, fa_33_p1
  and and_46 (and_46_out, B[3], A[2]);
  and and_47 (and_47_out, B[6], A[0]);
  HA ha_3 (.A(fa_38_p3), .B(and_47_out), .S(P[6]), .Cout(fa_35_p1));
  and and_48 (and_48_out, B[1], A[3]);
  // FA fa_41: pin names not known; wires that end beside it: fa_41_p1, and_46_out, fa_41_p3, fa_40_p3, fa_36_p1
  and and_49 (and_49_out, B[4], A[1]);
  // FA fa_42: pin names not known; wires that end beside it: fa_42_p1, fa_41_p3, fa_42_p3, and_49_out, fa_37_p1
  and and_50 (and_50_out, B[5], A[0]);
  HA ha_4 (.A(and_50_out), .B(fa_42_p3), .S(P[5]), .Cout(fa_38_p1));
  and and_51 (and_51_out, B[0], A[4]);
  // FA fa_43: pin names not known; wires that end beside it: fa_43_p1, and_48_out, fa_43_p3, and_51_out, fa_39_p1
  and and_52 (and_52_out, B[2], A[2]);
  // FA fa_44: pin names not known; wires that end beside it: fa_44_p1, fa_43_p3, fa_44_p3, and_52_out, fa_40_p1
  and and_53 (and_53_out, B[3], A[1]);
  // FA fa_45: pin names not known; wires that end beside it: fa_45_p1, and_53_out, fa_45_p3, fa_44_p3, fa_41_p1
  and and_54 (and_54_out, B[1], A[2]);
  // FA fa_46: pin names not known; wires that end beside it: fa_46_p1, and_54_out, fa_46_p3, fa_46_p4, fa_43_p1
  // FA fa_47: pin names not known; wires that end beside it: fa_47_p1, fa_46_p3, fa_47_p3, fa_47_p4, fa_44_p1
  and and_55 (and_55_out, B[4], A[0]);
  HA ha_5 (.A(and_55_out), .B(fa_45_p3), .S(P[4]), .Cout(fa_42_p1));
  and and_56 (fa_46_p4, B[0], A[3]);
  and and_57 (fa_47_p4, B[2], A[1]);
  and and_58 (and_58_out, B[3], A[0]);
  HA ha_6 (.A(fa_47_p3), .B(and_58_out), .S(P[3]), .Cout(fa_45_p1));
  and and_59 (and_59_out, B[0], A[2]);
  and and_60 (and_60_out, B[1], A[1]);
  // FA fa_48: pin names not known; wires that end beside it: fa_48_p1, and_60_out, fa_48_p3, and_59_out, fa_46_p1
  and and_61 (and_61_out, B[2], A[0]);
  HA ha_7 (.A(and_61_out), .B(fa_48_p3), .S(P[2]), .Cout(fa_47_p1));
  and and_62 (and_62_out, B[0], A[1]);
  and and_63 (and_63_out, B[1], A[0]);
  HA ha_8 (.A(and_62_out), .B(and_63_out), .S(P[1]), .Cout(fa_48_p1));
  and and_64 (P[0], B[0], A[0]);
endmodule
