// Digital circuit somador8bits.dig as structural Verilog
module somador8bits (
  input  [7:0] A,
  input  [7:0] B,
  output [7:0] S
);

  wire C1_cout, C2_cout, C3_cout, C4_cout, C5_cout, C6_cout, C7_cout, C8_cout;

  SOMA1BIT C1 (.a(A[0]), .b(B[0]), .Cin(1'b0), .Cout(C1_cout), .S(S[0]));
  SOMA1BIT C2 (.a(A[1]), .b(B[1]), .Cin(C1_cout), .Cout(C2_cout), .S(S[1]));
  SOMA1BIT C3 (.a(A[2]), .b(B[2]), .Cin(C2_cout), .Cout(C3_cout), .S(S[2]));
  SOMA1BIT C4 (.a(A[3]), .b(B[3]), .Cin(C3_cout), .Cout(C4_cout), .S(S[3]));
  SOMA1BIT C5 (.a(A[4]), .b(B[4]), .Cin(C4_cout), .Cout(C5_cout), .S(S[4]));
  SOMA1BIT C6 (.a(A[5]), .b(B[5]), .Cin(C5_cout), .Cout(C6_cout), .S(S[5]));
  SOMA1BIT C7 (.a(A[6]), .b(B[6]), .Cin(C6_cout), .Cout(C7_cout), .S(S[6]));
  SOMA1BIT C8 (.a(A[7]), .b(B[7]), .Cin(C7_cout), .Cout(C8_cout), .S(S[7]));
  // also tied to GND on the sheet: C8_cout

  // Other names for the same wires on the sheet: a2 = A[1]; a4 = A[2]; a8 = A[3]; a16 = A[4]; a32 = A[5]; a64 = A[6];
  //   a128 = A[7]; b2 = B[1]; b4 = B[2]; b8 = B[3]; b16 = B[4]; b32 = B[5]; b64 = B[6]; b128 = B[7]; s2 = S[1];
  //   s4 = S[2]; s8 = S[3]; s16 = S[4]; s32 = S[5]; s64 = S[6]; s128 = S[7]
endmodule
