// Digital circuit subrestore.dig as structural Verilog
module subrestore (
  input  A,
  input  B,
  input  Cin,
  input  S,
  output R,
  output Cout
);

  wire bnot, s_t;

  not not_1 (bnot, B);
  SOMA1BIT soma1bit_1 (.a(A), .b(bnot), .Cin(Cin), .Cout(Cout), .S(s_t));
  Multiplexer multiplexer_1 (.sel(S), .in_0(A), .in_1(s_t), .out(R));
endmodule
