// Digital circuit subtrator8bits.dig as structural Verilog
module subtrator8bits (
  input  [7:0] B,
  input  [7:0] A,
  output [7:0] S
);

  wire subtrator1bit_1_cout, subtrator1bit_2_cout, subtrator1bit_3_cout, subtrator1bit_4_cout,
       subtrator1bit_5_cout, subtrator1bit_6_cout, subtrator1bit_7_cout, subtrator1bit_8_cout;

  subtrator1bit subtrator1bit_1 (.A(A[0]), .B(B[0]), .C(1'b0), .S(S[0]), .Cout(subtrator1bit_1_cout));
  subtrator1bit subtrator1bit_2 (.A(A[1]), .B(B[1]), .C(subtrator1bit_1_cout), .S(S[1]), .Cout(subtrator1bit_2_cout));
  subtrator1bit subtrator1bit_3 (.A(A[2]), .B(B[2]), .C(subtrator1bit_2_cout), .S(S[2]), .Cout(subtrator1bit_3_cout));
  subtrator1bit subtrator1bit_4 (.A(A[3]), .B(B[3]), .C(subtrator1bit_3_cout), .S(S[3]), .Cout(subtrator1bit_4_cout));
  subtrator1bit subtrator1bit_5 (.A(A[4]), .B(B[4]), .C(subtrator1bit_4_cout), .S(S[4]), .Cout(subtrator1bit_5_cout));
  subtrator1bit subtrator1bit_6 (.A(A[5]), .B(B[5]), .C(subtrator1bit_5_cout), .S(S[5]), .Cout(subtrator1bit_6_cout));
  subtrator1bit subtrator1bit_7 (.A(A[6]), .B(B[6]), .C(subtrator1bit_6_cout), .S(S[6]), .Cout(subtrator1bit_7_cout));
  subtrator1bit subtrator1bit_8 (.A(A[7]), .B(B[7]), .C(subtrator1bit_7_cout), .S(S[7]), .Cout(subtrator1bit_8_cout));
  // also tied to GND on the sheet: subtrator1bit_8_cout

  // Other names for the same wires on the sheet: a2 = A[1]; a4 = A[2]; a8 = A[3]; a16 = A[4]; a32 = A[5]; a64 = A[6];
  //   a128 = A[7]; b2 = B[1]; b4 = B[2]; b8 = B[3]; b16 = B[4]; b32 = B[5]; b64 = B[6]; b128 = B[7]; s2 = S[1];
  //   s4 = S[2]; s8 = S[3]; s16 = S[4]; s32 = S[5]; s64 = S[6]; s128 = S[7]
endmodule
